// Digital circuit 4bit_CPU.dig as structural Verilog
module _4bit_CPU (
  input  [3:0] NxtMemAdrs,
  input  SysFlush,
  input  PC_CTRL,
  input  PC_Freeze,
  input  [3:0] A_in,
  input  A_CTRL,
  input  A_Freeze,
  input  [3:0] B_in,
  input  B_Freeze,
  input  IR_Freeze,
  input  Clock,
  input  RAM_Freeze,
  input  [3:0] Instruction,
  output [3:0] Output,
  output Z_Flag
);

  wire [3:0] A_q, B_q, IR_q, multiplexer_1_out, PC_output, RAM_dout;

  Multiplexer #(.Bits(4)) multiplexer_1 (.sel(A_CTRL), .in_0(A_in), .in_1(Output), .out(multiplexer_1_out));
  _4bit_PC PC (
    .PC_IN(NxtMemAdrs), .Control(PC_CTRL), .Clock(Clock), .setClear(SysFlush), .setLoad(PC_Freeze),
    .Output(PC_output));
  _4bit_register A (
    .In(multiplexer_1_out), .Clock(Clock), .setClear(SysFlush), .setLoad(A_Freeze), .Q(A_q));  // open: Q_2
  _4bit_register B (.In(B_in), .Clock(Clock), .setClear(SysFlush), .setLoad(B_Freeze), .Q(B_q));  // open: Q_2
  _4bit_register IR (.In(RAM_dout), .Clock(Clock), .setClear(SysFlush), .setLoad(IR_Freeze), .Q(IR_q));  // open: Q_2
  _4Bit_Ram_Module RAM (
    .Read_Write(Clock), .MemAddress(PC_output), .Data(Instruction), .setClear(SysFlush),
    .setLoad(RAM_Freeze), .Dout(RAM_dout));
  _4bit_ALU _4bit_alu_1 (.A(A_q), .B(B_q), .Control(IR_q[2:0]), .Output(Output), .Zero_Flag(Z_Flag));
endmodule
